# Fritzing sketch Diagram (saved by Fritzing 0.9.9b)
breadboards: 1

parts:
  Part1 = Arduino Uno (Rev3) - ICSP
  Pololu_A1 = Pololu A4988 [package=SO16]
  Pololu_A2 = Pololu A4988 [package=SO16]
  Pololu_A3 = Pololu A4988 [package=SO16]
  M2 = Stepper Motor - Bipolar
  M3 = Stepper Motor - Bipolar
  M4 = Stepper Motor - Bipolar
  J2 = Power Jack [package=power_jack_pth_lock]

nets:
  VDD: Part1.5V, Pololu_A1.VDD, Pololu_A2.VDD, Pololu_A3.VDD
  N1: Part1.GND, Pololu_A1.GND#8, Pololu_A2.GND#8, Pololu_A3.GND#8
  N2: Pololu_A1.RESET, Pololu_A1.SLEEP
  N3: Pololu_A1.1B, M2.D
  N4: Pololu_A1.1A, M2.B
  N5: Pololu_A1.2A, M2.C
  N6: Pololu_A1.2B, M2.A
  N7: Pololu_A1.GND#14, Pololu_A2.GND#14, Pololu_A3.GND#14, J2.GND
  N8: Pololu_A1.VMOT, Pololu_A2.VMOT, Pololu_A3.VMOT, J2.PWR
  N9: Pololu_A2.RESET, Pololu_A2.SLEEP
  N10: Pololu_A2.1B, M4.D
  N11: Pololu_A2.1A, M4.B
  N12: Pololu_A2.2A, M4.C
  N13: Pololu_A2.2B, M4.A
  N14: Pololu_A3.RESET, Pololu_A3.SLEEP
  N15: Pololu_A3.1B, M3.D
  N16: Pololu_A3.1A, M3.B
  N17: Pololu_A3.2A, M3.C
  N18: Pololu_A3.2B, M3.A

notes:
  2
  1
  3
  Motor Power Source
